# Fritzing sketch NodeMCU lolin Temperature relay lcd (saved by Fritzing 0.9.3b)
breadboards: 1

parts:
  U1 = NodeMCU V3.0
  C1 = Electrolytic Capacitor [capacitance=1µF package="100 mil [THT, electrolytic]"]
  NEOPIXEL1 = Neopixel Strip -- Black (30/m) [part_number=1376]
  ZS-042_RTC1 = ZS-042 RTC Module
  R1 = Resistor [tolerance=±5% resistance=1k package="2512 [SMD]"]
  JACK1 = 2.1mm Barrel Jack with Terminal Block
  74HC245N = IC, DIP package, 20 pins [chip_label=74HC245N]

nets:
  N1: U1.D1, ZS-042_RTC1.SCL
  N2: U1.D2, ZS-042_RTC1.SDA
  N3: U1.D3, 74HC245N.pin18
  3V3: U1.3V3, ZS-042_RTC1.VCC
  N4: U1.GND#6, U1.GND#13, U1.GND#16, U1.GND#33
  VIN: U1.Vin, C1.+, NEOPIXEL1.+5V, JACK1.POS, 74HC245N.pin20
  GND: C1.-, NEOPIXEL1.GND, ZS-042_RTC1.GND, JACK1.NEG, 74HC245N.pin1, 74HC245N.pin10, 74HC245N.pin19
  N5: NEOPIXEL1.Din, R1.Pin_1
  N6: R1.Pin_0, 74HC245N.pin2

custom parts:
  NodeMCU V3.0: ESP8266 based NodeMCU
  Neopixel Strip -- Black (30/m): These NeoPixel strips have 30 digitally-addressable pixel LEDs per meter and are very affordable and are only 12.5 mm wide, 10 mm if you remove the strip from the casing.

// code stored in the sketch: ESP8266_NeoPixel_Dashboard-V2.ino
//This one includes all the other includes, this makes sure that the main file is not messy.
#include "_external.h"


void setup() {

  //Init all the Subsystems.
  Serial.begin(115200);
  matrixInit();
  fxInit();
  rtcInit();
  timeInit();
  timerInit();
  blynkInit();
  
}

void loop() {

//Check if Blynk is connected, to make sure that the code doesn't become blocking.
  if (Blynk.connected())
  {
    blynkConnected = true;
    Blynk.run();
    pingCheck = false;
  }
  else
  {
    blynkConnected = false;
  }
  //Run the Timer.
  timer.run();
}

// code stored in the sketch: NodemcuTemperatureRelayLcd.ino
/********************** LYBRARY ****************************/

#define BLYNK_PRINT Serial // Comment this out to disable prints and save space


#include <ESP8266WiFi.h>
#include <BlynkSimpleEsp8266.h>
#include <OneWire.h>
#include <DallasTemperature.h>
#include <LiquidCrystal_I2C.h>

/* TIMER */
#include <SimpleTimer.h>
SimpleTimer timer;

/********************** BLYNK ACCOUNT ****************************/
char auth[] = "BLYNK_TOKEN";
char ssid[] = "SSID";
char pass[] = "PASS";


/********************** HARDWARE ****************************/
// Temperature sensor full ID, including family code and CRC
// use OneWire Scanner to get the address
DeviceAddress tempSensor = { 0x28, 0xFF, 0x64, 0x1D, 0x8F, 0x87, 0x95, 0xB1 };

// Pin used for the OneWire interface
#define ONE_WIRE_BUS 14 //pin D5 nodemcu Lolin v3

LiquidCrystal_I2C lcd(0x27, 16, 2); //LCD address and type.
//D2 = SDA D1 = SCL

/**************BIG CHAR*********************************************/


/********************** TEMPERATURE DEF****************************/
OneWire oneWire(ONE_WIRE_BUS);
DallasTemperature DS18B20(&oneWire);
float temp;

/********************** SETUP ****************************/
void setup()
{
  // Debug console
  Serial.begin(9600);
  Blynk.begin(auth, ssid, pass, IPAddress(188,166,206,43), 8080); //use other method to connect to blynk server
  DS18B20.begin();
  timer.setInterval(15000L, getSendData);
  Blynk.syncAll();

  pinMode(2, OUTPUT);
  
  lcd.init();
  lcd.backlight();
  lcd.clear();

}

/********************** LOOP ****************************/
void loop()
{
  Blynk.run();
  timer.run();
}

/********************** Send Sensor data to Blynk ****************************/
void getSendData()
{
  DS18B20.requestTemperatures(); 
  temp = DS18B20.getTempCByIndex(0);
  Serial.println(temp);
  Blynk.virtualWrite(10, temp); //virtual pin V10
  
  lcd.setCursor(0, 0);
  lcd.print("Temp:");
  lcd.setCursor(6,0);
  lcd.print(temp);
  lcd.setCursor(12,0);
  lcd.print("'C");
}
